# Fritzing sketch Schematic (saved by Fritzing 0.9.6b)

parts:
  Part2 = Arduino Mega 2560 (Rev3)
  U1 = RS232 Transceiver [package=so016]
  X1 = DB9 Connector [package=db9]  # not connected
  J1 = Camdenboss CTB0158-3 [part_number=CTB0158-3 package=THT]  # not connected

nets:
  N1: Part2.D18/TX1, U1.C1+
  N2: Part2.D17_PWM/RX2, U1.V+
  N3: Part2.GND, U1.C1-
